// Logisim project trabalho5.circ as structural Verilog: 7 circuits, main circuit main
module main (
  input  [15:0] A,
  input  [15:0] B,
  input  [15:0] C,
  input  [7:0] X,
  input  start,
  input  clock,
  input  reset,
  output [15:0] resultado
);

  wire quadratic_eq_1_pronto;

  quadratic_eq quadratic_eq_1 (
    .pronto(quadratic_eq_1_pronto), .resultado(resultado), .clock(clock), .reset(reset), .start(start),
    .X(X), .A(A), .B(B), .C(C));
  LED finalizado (.in(quadratic_eq_1_pronto));
endmodule

module quadratic_eq (
  input  [7:0] X,
  input  [15:0] A,
  input  [15:0] B,
  input  [15:0] C,
  input  start,
  input  clock,
  input  reset,
  output [15:0] resultado,
  output pronto
);

  wire bc_1_h, bc_1_lh, bc_1_ll, bc_1_lx;
  wire [1:0] bc_1_m0, bc_1_m1, bc_1_m2;

  BC bc_1 (
    .H(bc_1_h), .pronto(pronto), .LH(bc_1_lh), .LL(bc_1_ll), .LX(bc_1_lx), .M0(bc_1_m0), .M1(bc_1_m1),
    .M2(bc_1_m2), .start(start), .clock(clock), .reset(reset));
  BO bo_1 (
    .resultado(resultado), .load_X(bc_1_lx), .X(X), .H(bc_1_h), .M1(bc_1_m1), .load_L(bc_1_ll),
    .pronto(pronto), .A(A), .M2(bc_1_m2), .B(B), .M0(bc_1_m0), .C(C), .load_H(bc_1_lh), .clock(clock),
    .reset(reset));

  // Notes on the sheet:
  //   X: pull=up
endmodule

module BC (
  input  start,
  input  clock,
  input  reset,
  output LX,
  output LH,
  output LL,
  output [1:0] M0,
  output [1:0] M1,
  output [1:0] M2,
  output H,
  output pronto
);

  wire and_1_out, and_2_out, and_3_out, and_4_out, and_5_out, and_6_out, and_7_out, and_8_out, and_9_out,
       and_10_out, and_11_out, and_12_out, and_15_out, and_16_out, and_17_out, and_18_out, and_19_out,
       and_20_out, and_21_out, and_22_out, and_23_out, and_24_out, and_25_out, and_26_out, and_27_out,
       and_28_out, and_29_out, and_30_out, and_31_out, and_32_out, and_33_out, and_34_out, and_35_out,
       and_36_out, or_1_out, or_2_out, or_3_out, or_4_out, Q0_q, Q1_q, Q2_q, Q3_q;

  and and_1 (and_1_out, Q1_q, ~Q0_q);  // AND_Gate
  and and_2 (and_2_out, Q2_q, ~Q0_q);  // AND_Gate
  and and_3 (and_3_out, Q3_q, ~Q0_q);  // AND_Gate
  and and_4 (and_4_out, start, ~Q0_q);  // AND_Gate
  and and_5 (and_5_out, ~Q1_q, Q0_q);  // AND_Gate
  and and_6 (and_6_out, Q1_q, ~Q0_q);  // AND_Gate
  and and_7 (and_7_out, Q2_q, ~Q1_q);  // AND_Gate
  and and_8 (and_8_out, Q2_q, ~Q0_q);  // AND_Gate
  and and_9 (and_9_out, ~Q3_q, ~Q2_q, Q1_q, Q0_q);  // AND_Gate
  and and_10 (and_10_out, Q3_q, ~Q1_q);  // AND_Gate
  and and_11 (and_11_out, Q3_q, ~Q0_q);  // AND_Gate
  and and_12 (and_12_out, Q2_q, Q1_q, Q0_q);
  or or_1 (or_1_out, and_5_out, and_6_out);
  or or_2 (or_2_out, and_7_out, and_8_out, and_9_out);
  or or_3 (or_3_out, and_10_out, and_11_out, and_12_out);
  or or_4 (or_4_out, and_1_out, and_2_out, and_3_out, and_4_out);
  Register #(.width(1)) Q0 (.D(or_4_out), .clk(clock), .Q(Q0_q), .clr(reset));  // open: en
  Register #(.width(1)) Q1 (.D(or_1_out), .clk(clock), .Q(Q1_q), .clr(reset));  // open: en
  Register #(.width(1)) Q2 (.D(or_2_out), .clk(clock), .Q(Q2_q), .clr(reset));  // open: en
  Register #(.width(1)) Q3 (.D(or_3_out), .clk(clock), .Q(Q3_q), .clr(reset));  // open: en
  and and_13 (LX, ~Q3_q, ~Q2_q, ~Q1_q, ~Q0_q);  // AND_Gate
  and and_14 (LH, Q2_q, Q1_q, ~Q0_q);  // AND_Gate
  and and_15 (and_15_out, Q3_q, ~Q0_q);  // AND_Gate
  and and_16 (and_16_out, ~Q2_q, Q1_q, ~Q0_q);  // AND_Gate
  and and_17 (and_17_out, Q2_q, ~Q1_q, ~Q0_q);  // AND_Gate
  and and_18 (and_18_out, Q3_q, ~Q1_q, Q0_q);  // AND_Gate
  and and_19 (and_19_out, Q3_q, Q1_q, ~Q0_q);  // AND_Gate
  and and_20 (and_20_out, Q2_q, ~Q1_q, Q0_q);  // AND_Gate
  and and_21 (and_21_out, Q2_q, Q1_q, ~Q0_q);  // AND_Gate
  and and_22 (and_22_out, Q3_q, ~Q1_q, Q0_q);  // AND_Gate
  and and_23 (and_23_out, Q3_q, Q1_q, ~Q0_q);  // AND_Gate
  and and_24 (and_24_out, Q2_q, ~Q1_q, ~Q0_q);  // AND_Gate
  and and_25 (and_25_out, ~Q3_q, ~Q2_q, Q1_q, Q0_q);  // AND_Gate
  and and_26 (and_26_out, Q3_q, ~Q1_q);  // AND_Gate
  and and_27 (and_27_out, Q3_q, ~Q0_q);  // AND_Gate
  and and_28 (and_28_out, ~Q3_q, Q1_q, Q0_q);  // AND_Gate
  and and_29 (and_29_out, Q2_q, ~Q1_q, ~Q0_q);  // AND_Gate
  and and_30 (and_30_out, Q2_q, Q1_q, Q0_q);
  and and_31 (and_31_out, Q3_q, ~Q1_q, ~Q0_q);  // AND_Gate
  and and_32 (and_32_out, ~Q3_q, ~Q2_q, ~Q1_q, Q0_q);  // AND_Gate
  and and_33 (and_33_out, ~Q3_q, ~Q2_q, Q1_q, ~Q0_q);  // AND_Gate
  and and_34 (and_34_out, Q2_q, ~Q0_q);  // AND_Gate
  and and_35 (and_35_out, ~Q3_q, ~Q1_q, Q0_q);  // AND_Gate
  and and_36 (and_36_out, ~Q3_q, ~Q2_q, Q1_q);  // AND_Gate
  and and_37 (pronto, Q3_q, Q1_q, Q0_q);
  or or_5 (LL, and_15_out, and_16_out, and_17_out);
  or or_6 (M0[1], and_18_out, and_19_out, and_20_out, and_21_out);
  or or_7 (M0[0], and_22_out, and_23_out, and_24_out, and_25_out);
  or or_8 (M1[1], and_26_out, and_27_out, and_28_out, and_29_out);
  or or_9 (M2[1], and_30_out, and_31_out);
  or or_10 (M2[0], and_30_out, and_31_out, and_32_out, and_33_out);
  or or_11 (H, and_34_out, and_35_out, and_36_out);

  assign M1[0] = 1'b0;
endmodule

module BO (
  input  clock,
  input  [7:0] X,
  input  reset,
  input  load_X,
  input  [15:0] A,
  input  [15:0] B,
  input  [15:0] C,
  input  [1:0] M0,
  input  [1:0] M1,
  input  [1:0] M2,
  input  H,
  input  load_H,
  input  load_L,
  input  pronto,
  output [15:0] resultado
);

  wire [15:0] multiplexer_1_out, multiplexer_3_out, multiplexer_4_out, reg_16b_1_saida, reg_16b_2_saida,
       reg_x_1_saida, ula_1_resultado;

  Reg_X reg_x_1 (.saida(reg_x_1_saida), .clock(clock), .reset(reset), .X(X), .load(load_X));
  Multiplexer #(.select(2), .width(16)) multiplexer_1 (
    .in0(reg_x_1_saida), .in1(multiplexer_3_out), .in2(reg_16b_1_saida), .in3(reg_16b_2_saida),
    .out(multiplexer_1_out), .sel(M1));
  Reg_16b reg_16b_1 (.saida(reg_16b_1_saida), .clock(clock), .reset(reset), .load(load_L), .in_1(ula_1_resultado));
  Multiplexer #(.width(16)) multiplexer_2 (.in0({16{1'b0}}), .in1(reg_16b_1_saida), .out(resultado), .sel(pronto));
  Multiplexer #(.select(2), .width(16)) multiplexer_3 (
    .in1(A), .in2(B), .in3(C), .out(multiplexer_3_out), .sel(M0));  // open: in0
  Multiplexer #(.select(2), .width(16)) multiplexer_4 (
    .in0(multiplexer_3_out), .in1(reg_x_1_saida), .in2(reg_16b_1_saida), .in3(reg_16b_2_saida),
    .out(multiplexer_4_out), .sel(M2));
  ULA ula_1 (.resultado(ula_1_resultado), .M2(multiplexer_4_out), .M1(multiplexer_1_out), .H(H));
  Reg_16b reg_16b_2 (.saida(reg_16b_2_saida), .clock(clock), .reset(reset), .load(load_H), .in_1(ula_1_resultado));

  // Notes on the sheet:
  //   X: pull=up
  //   00 - X
  //   01 - M0
  //   10 - resultado
  //   11 - Reg_H
  //   Reg_L
  //   0 - retorna 0
  //   1 - retorna resultado
  //   01 - A
  //   10 - B
  //   11 - C
  //   00 - M0
  //   01 - X
  //   10 - resultado
  //   11 - Reg_H
  //   Reg_H
endmodule

module Reg_X (
  input  [7:0] X,
  input  load,
  input  clock,
  input  reset,
  output [15:0] saida
);

  Register register_1 (.D(X), .en(load), .clk(clock), .Q(saida[7:0]), .clr(reset));

  assign saida[15:8] = {8{1'b0}};
endmodule

module ULA (
  input  [15:0] M1,
  input  [15:0] M2,
  input  H,
  output [15:0] resultado
);

  wire [15:0] adder_1_out, multiplier_1_out;

  Adder #(.width(16)) adder_1 (.a(M1), .b(M2), .out(adder_1_out));  // open: cin, cout
  Multiplier #(.width(16)) multiplier_1 (.a(M1), .b(M2), .out(multiplier_1_out));  // open: cin, cout
  Multiplexer #(.width(16)) multiplexer_1 (.in0(adder_1_out), .in1(multiplier_1_out), .out(resultado), .sel(H));
endmodule

module Reg_16b (
  input  [15:0] in_1,
  input  load,
  input  clock,
  input  reset,
  output [15:0] saida
);

  Register #(.width(16)) register_1 (.D(in_1), .en(load), .clk(clock), .Q(saida), .clr(reset));
endmodule
